# Fritzing sketch circuit_diagram (saved by Fritzing 0.9.3b)
circuit board: 7.81982cm x 5.23208cm
breadboards: 1

parts:
  U1 = NodeMCU V1.0
  Squix1 = OLED 0.96" 128x64 I2C SSD1306
  M1 = fc-51 [package=THT]
  M2 = fc-51 [package=THT]
  Piezo1 = Piezo Speaker - PC Mount [part_number=COM-07950]
  S1 = Pushbutton [package="[THT]"]
  S2 = Pushbutton [package="[THT]"]

nets:
  N1: U1.D1, Squix1.SCL
  N2: U1.D2, Squix1.SCA
  GND: U1.D3, U1.D4, U1.GND, Squix1.GND, M1.pin2, M2.pin2, Piezo1.GND, S1.Pin_1, S1.Pin_2, S1.Pin_3, S1.Pin_4, S2.Pin_1, S2.Pin_2, S2.Pin_3, S2.Pin_4
  3V3: U1.3V3, Squix1.VCC, M1.pin3, M2.pin3
  N3: U1.D5, Piezo1.VCC
  N4: U1.D6, M1.pin1
  N5: U1.D7, M2.pin1

custom parts:
  NodeMCU V1.0: ESP8266 based NodeMCU
  Piezo Speaker - PC Mount: This is a small 12mm round speaker that operates around the audible 2kHz range. You can use these speakers to create simple music or user interfaces. Each speaker is PTH solderable and requires an operating voltage of 3.5-5V with a mean current of 35mA max. These speakers also have a typical sound output of 95 dBA and a coil resistance of 42 ±6.3 ohms.
